// Logisim project Proprieta2BertoldoMatteo.circ as structural Verilog: 1 circuit, main circuit main
module main (
  input  A,
  input  A_2,
  input  B,
  input  B_2,
  input  C,
  input  C_2,
  input  A_3,
  input  A_4,
  input  B_3,
  input  B_4,
  input  C_3,
  input  C_4,
  input  A_5,
  input  A_6,
  input  B_5,
  input  B_6,
  input  A_7,
  input  A_8,
  input  in_19,
  input  in_20,
  input  in_21,
  input  in_22,
  input  in_23,
  input  in_24,
  input  in_25,
  input  in_26,
  input  in_27,
  input  A_9,
  input  B_7,
  input  Ping,
  input  [3:0] INPUT,
  input  A_10,
  input  B_8,
  input  A_11,
  input  B_9,
  input  [3:0] in_36,
  input  [3:0] B_10,
  input  D0,
  input  D1,
  input  D2,
  input  D3,
  input  D4,
  input  D5,
  input  D6,
  input  D7,
  input  in_46,
  input  CLEAR,
  input  SET,
  input  CLEAR_2,
  input  SET_2,
  input  in_51,
  input  in_52,
  output A_B,
  output AB
);

  wire AB_out, AC_out, and_1_out, and_2_out, and_3_out, and_4_out, and_5_out, and_6_out, and_7_out,
       and_8_out, and_9_out, and_10_out, and_11_out, and_12_out, and_13_out, and_14_out, and_15_out,
       and_16_out, and_17_out, and_18_out, and_19_out, and_20_out, and_21_out, and_22_out, and_23_out,
       and_24_out, and_25_out, and_26_out, and_27_out, and_28_out, and_29_out, and_30_out, and_31_out,
       and_32_out, and_33_out, and_34_out, and_35_out, and_36_out, and_37_out, and_38_out, and_39_out,
       and_40_out, and_41_out, clock_1_out, clock_2_out, clock_3_out, nand_1_out, nor_1_out, nor_2_out,
       nor_3_out, nor_4_out, nor_5_out, nor_6_out, nor_7_out, nor_8_out, nor_9_out, nor_10_out, nor_11_out,
       nor_12_out, not_1_out, not_2_out, not_3_out, not_4_out, not_5_out, not_6_out, not_7_out, not_8_out,
       not_13_out, not_14_out, not_15_out, not_16_out, not_17_out, not_18_out, not_19_out, or_1_out,
       or_2_out, or_3_out, or_4_out, or_5_out, or_6_out, or_7_out, or_8_out, or_9_out, or_10_out, or_11_out,
       or_12_out, or_13_out, or_14_out, or_15_out, or_16_out, or_17_out, xnor_1_out, xor_1_out, xor_2_out,
       xor_3_out, xor_4_out, xor_5_out, xor_6_out, xor_7_out, xor_8_out, xor_9_out;
  wire [3:0] not_12_out;

  not not_1 (not_1_out, in_46);
  or or_1 (or_1_out, B_3, C_3);
  not not_2 (not_2_out, in_19);
  not not_3 (not_3_out, in_21);
  not not_4 (not_4_out, A_9);
  not not_5 (not_5_out, B_9);
  not not_6 (not_6_out, A_11);
  not not_7 (not_7_out, A_11);
  not not_8 (not_8_out, B_9);
  and and_1 (and_1_out, D0, in_46);
  // Probe on and_9_out
  Clock clock_1 (.out(clock_1_out));
  Clock clock_2 (.out(clock_2_out));
  Clock clock_3 (.out(clock_3_out));
  and u_AB (AB_out, A, B);
  and AC (AC_out, A, C_2);
  or or_2 (or_2_out, A_5, B_5);
  // Probe on nand_1_out
  nand nand_1 (nand_1_out, in_19, in_21);
  or or_3 (or_3_out, not_2_out, not_3_out);
  xor xor_1 (xor_1_out, in_25, in_26);
  and and_2 (and_2_out, in_25, in_26);
  and and_3 (and_3_out, in_26, in_27);
  and and_4 (and_4_out, in_27, in_25);
  xor xor_2 (xor_2_out, A_9, B_7);
  not not_9 (not_12_out[3], INPUT[3]);
  not not_10 (not_12_out[2], INPUT[2]);
  not not_11 (not_12_out[1], INPUT[1]);
  not not_12 (not_12_out[0], INPUT[0]);
  and and_5 (and_5_out, B_9, A_11);
  and and_6 (and_6_out, not_5_out, not_6_out);
  and and_7 (and_7_out, B_9, not_7_out);
  and and_8 (and_8_out, not_8_out, A_11);
  and and_9 (and_9_out, not_1_out, D1);
  not not_13 (not_13_out, in_51);
  not not_14 (not_14_out, in_52);
  not not_15 (not_15_out, clock_3_out);
  // Probe on or_4_out
  or or_4 (or_4_out, AB_out, AC_out);
  // Probe on and_10_out
  and and_10 (and_10_out, A_3, or_1_out);
  // Probe on and_11_out
  and and_11 (and_11_out, A_5, or_2_out);
  // Probe on or_3_out
  // Probe on xor_3_out
  xor xor_3 (xor_3_out, in_23, in_24);
  // Probe on and_12_out
  and and_12 (and_12_out, in_23, in_24);
  // Probe on xor_4_out
  xor xor_4 (xor_4_out, xor_2_out, Ping);
  and and_13 (and_13_out, not_4_out, B_7);
  and and_14 (and_14_out, not_4_out, Ping);
  and and_15 (and_15_out, B_7, Ping);
  // Probe on not_12_out
  // Probe on and_7_out
  // Probe on and_8_out
  and and_16 (and_16_out, D1, in_46);
  or or_5 (or_5_out, and_1_out, and_23_out);
  // Probe on or_5_out
  nor nor_1 (nor_1_out, CLEAR, nor_2_out);
  nor nor_2 (nor_2_out, nor_1_out, SET);
  and and_17 (and_17_out, CLEAR_2, clock_1_out);
  and and_18 (and_18_out, clock_1_out, SET_2);
  and and_19 (and_19_out, clock_2_out, not_13_out);
  and and_20 (and_20_out, clock_2_out, in_51);
  and and_21 (and_21_out, clock_3_out, in_52);
  and and_22 (and_22_out, clock_3_out, not_14_out);
  // Probe on xor_5_out
  xor xor_5 (xor_5_out, xor_1_out, in_27);
  or or_6 (or_6_out, and_2_out, and_3_out, and_4_out);
  or or_7 (or_7_out, and_13_out, and_14_out, and_15_out);
  or or_8 (or_8_out, and_5_out, and_6_out);
  and and_23 (and_23_out, not_1_out, D2);
  or or_9 (or_9_out, and_16_out, and_25_out);
  // Probe on or_9_out
  // Probe on or_6_out
  // Probe on or_7_out
  // Probe on or_8_out
  xor xor_6 (xor_6_out, in_36[3], B_10[3]);
  xor xor_7 (xor_7_out, in_36[2], B_10[2]);
  xor xor_8 (xor_8_out, in_36[1], B_10[1]);
  xor xor_9 (xor_9_out, in_36[0], B_10[0]);
  and and_24 (and_24_out, D2, in_46);
  and and_25 (and_25_out, not_1_out, D3);
  // Probe on nor_1_out
  // Probe on nor_2_out
  nor nor_3 (nor_3_out, and_17_out, nor_4_out);
  nor nor_4 (nor_4_out, nor_3_out, and_18_out);
  nor nor_5 (nor_5_out, and_19_out, nor_6_out);
  nor nor_6 (nor_6_out, nor_5_out, and_20_out);
  nor nor_7 (nor_7_out, and_21_out, nor_8_out);
  nor nor_8 (nor_8_out, nor_7_out, and_22_out);
  and and_26 (and_26_out, D3, in_46);
  or or_10 (or_10_out, and_24_out, and_27_out);
  // Probe on or_10_out
  // Probe on nor_4_out
  nor nor_9 (nor_9_out, in_20, in_22);
  not not_16 (not_16_out, in_20);
  not not_17 (not_17_out, in_22);
  and and_27 (and_27_out, not_1_out, D4);
  // Probe on nor_3_out
  // Probe on nor_5_out
  // Probe on nor_6_out
  and and_28 (and_28_out, B_2, C);
  or or_11 (or_11_out, A_4, B_4);
  or or_12 (or_12_out, A_4, C_4);
  and and_29 (and_29_out, A_6, B_6);
  // Probe on nor_9_out
  and and_30 (and_30_out, not_16_out, not_17_out);
  not not_18 (not_18_out, A_10);
  not not_19 (not_19_out, B_8);
  // Probe on nor_10_out
  nor nor_10 (nor_10_out, xor_6_out, xor_7_out, xor_8_out, xor_9_out);
  and and_31 (and_31_out, D4, in_46);
  or or_13 (or_13_out, and_26_out, and_34_out);
  // Probe on or_13_out
  or or_14 (or_14_out, A_2, and_28_out);
  or or_15 (or_15_out, A_6, and_29_out);
  // Probe on and_30_out
  xnor xnor_1 (xnor_1_out, B_8, A_10);
  and and_32 (and_32_out, B_8, not_18_out);
  and and_33 (and_33_out, not_19_out, A_10);
  and and_34 (and_34_out, not_1_out, D5);
  and and_35 (and_35_out, D5, in_46);
  or or_16 (or_16_out, and_31_out, and_37_out);
  // Probe on or_16_out
  // Probe on or_14_out
  // Probe on and_36_out
  and and_36 (and_36_out, or_11_out, or_12_out);
  // Probe on or_15_out
  // Probe on xnor_1_out
  // Probe on and_32_out
  // Probe on and_33_out
  and and_37 (and_37_out, not_1_out, D6);
  and and_38 (and_38_out, not_15_out, nor_7_out);
  and and_39 (and_39_out, nor_8_out, not_15_out);
  and and_40 (and_40_out, D6, in_46);
  or or_17 (or_17_out, and_35_out, and_41_out);
  // Probe on or_17_out
  and and_41 (and_41_out, not_1_out, D7);
  // Probe on and_40_out
  nor nor_11 (nor_11_out, and_38_out, nor_12_out);
  nor nor_12 (nor_12_out, nor_11_out, and_39_out);
  // Probe on nor_11_out
  // Probe on nor_12_out

  assign A_B = A_7;
  assign AB = A_8;

  // Notes on the sheet:
  //   A
  //   CLOCK
  //   CLOCK
  //   D (S CON C)
  //   CLOCK
  //   D (S CON C)
  //   B+C
  //   B
  //   A
  //   B'
  //   A'
  //   B
  //   A'
  //   B'
  //   A
  //   S0
  //   CLK'
  //   INGRESSO
  //   DEL CLOCK
  //   Proprietà distributiva della porta OR
  //   A(B+C)=AB+AC
  //   A(B+C)
  //   Proprietà di assorbimento della porta AND
  //   A(A+B)=A
  //   Proprietà DE MORGAN forma AND
  //   (AB)'=A'+B'
  //   COMPARATORE DI 2 BIT (a=b - a<b - a>b)
  //   PASSO 1 : Q DIVENTA 1 QUANDO SET È IMPOSTATO A 1
  //   PASSO 2 : Q RICORDA 1 QUANDO SET È REIMPOSTATO A 0
  //   PASSO 3 : Q RITORNA A 0 QUANDO CLEAR È IMPOSTATO A 1
  //   PASSO 4: Q RESTA 0 QUANDO CLEAR È REIMPOSTATO A 0
  //   DM
  //   D'M
  //   AB+AC
  //   A(A+B)
  //   (AB)'
  //   A<B
  //   A>B
  //   S1
  //   LATCH SC SINCRONO CON CLOCK
  //   SOLO QUANDO IL CLOCK È ALTO LE PORTE AND FANNO PASSARE GLI INPUT
  //   UTILE NEI CASI IN CUI HO DIVERSI COMPONENTI SOTTO IL CONTROLLO DEL MEDESIMO CLOCK
  //   ATTENZIONE!!! SU DIVERSI CIRCUITI INTEGRATI PROBABILE PROBLEMA RITARDO SEGNALE
  //   LATCH TIPO D (UNICO INGRESSO CHE INCLUDE SET E RESET O CLEAR)
  //   MEMORIZZA IL VALORE PRESENTE IN D
  //   SOLO QUANDO IL CLOCK È ALTO
  //   RISOLVE IL PROBLEMA DEL RITARDO PROPAGAZIONE SEGNALE
  //   FLIP-FLOP DI TIPO D (MASTER-SLAVE) - NEI FLIP-FLOP LA MEMORIZZAZIONE 
  //   MASTER
  //   PUÒ RAGGIUNGERE L'USCITA STABILE DI LATCH MASTER
  //   LATCH SLAVE E DI RAGGOIUNGERE L'USCITA Q
  //   PASSO 4: SI POTREBBE AVERE LA FALSA IMPRESSIONE CHE IN QUESTO MOMENTO 
  //   L'USCITA Q HA VALORE 1 A CAUSA DEL FATTO CHE LO STATO DI D SIA 1
  //   MA SAPPIAMO CHE NON Ë COSÌ ( ORA L'INGRESSO Ë CHIUSO) E INFATTI,
  //   AB+AC
  //   A(B+C)
  //   A'+B'
  //   DIFFERENZA COMPLETA CON GESTIONE DEL RIPORTO IN INGRESSO E USCITA
  //   COMPLEMENTO A 1 DI 4 BIT IN INPUT
  //   SPLITTER PERMETTE DI SUDDIVIDERE O RAGGRUPPARE UN BUS IN GRUPPI DISTINTI DI BIT
  //   COMPARATORE DI STRINGHE DI 4 BIT
  //   S2
  //   AVVIENE SUL FRONTE DI DISCESA O IN SALITA O IN DISCESA
  //   MASTER-SLAVE = APPENA APRO INGRESSO CON LE PORTE AND, CHIUDO L'USCITA E VICEVERSA
  //   QUANDO IL CLOCK E' SUL FRONTE IN SALITA NEL MASTER PASSA IL SEGNALE MA NON ARRIVA
  //   ALL'USCITA DELLO SLAVE, APPENA IL CLOCK E' NELLA FASEDI DISCESA IL SEGNALE ARRIVA NELLO SLAVE
  //   DM=DS
  //   BLOCCA L'INGRESSO DEL SEGNALE NELLA PARTE COMBINATORIA DI MASTER
  //   PASSO 2: IMPOSTO IL VALORE DI CLOCK A 1. ORA IL SEGNALE CHE PROVIENE DA D ( CHE Ë RIMASTO 1 )
  //   MA L'USCITA Ë BLOCCATA... IL SEGNALE NON SI PUÒ PROPAGARE IN LATCH SLAVE
  //   PASSO 3: REIMPOSTO IL VALORE DI CLOCK A 0. FRONTE DI DISCESA, ORA IL SEGNALE
  //   PROVENIENTE DA D Ë STABILIZZATO IN Q DI MASTER ED Ë LIBERO 
  //   (STATO CORRENTE : INGRESSO BLOCCATO / USCITA APERTA) DI PROPAGARSI IN 
  //    SE IMPOSTO IL VALORE DI DI A 0, L'USCITA DEL CIRCUITO RIMANE STABILE AL
  //   VALORE CHE HA ASSUNTO DURANTE L'ULTIMO FRONTE (OSSIA IL FRONTE DI DISCESA)
  //   S(SOMMA)= AXOR B
  //   FULL ADDER:SOMMA DUE BIT ( TIENE CONTO DEL RIPORTO IN INGRESSO E USCITA)
  //   A=B
  //   IMPLEMENTAZIONE DI UNO SHIFTER DA 8 BIT IN INGRESSO CON UN BIT DI SCELTA DEL VERSO (SX, DX)
  //   LACTH SC (SET-CLOCK O SR SET-CLEAR) ASINCRONO NON C'È CLOCK
  //   Q
  //   Q'
  //   QUESTO PER NON PROPAGARE IL SEGNALE A TUTTO IL CIRCUITO CONTEPORANEAMENTE
  //   Q'M = D'S
  //   PASSO 1: IMPOSTO IL VALORE DI D A 1, LO STATO DI D Ë PRONTO A FARSI MEMORIZZARE NELL'USCITA
  //   STABILE DI MASTER, MA QUESTO NON Ë POSSIBILE PERCHË IL CLOCK Ë BASSE E IL PRIMO CANCELLO"
  //   IN QUESTO MOMENTO ( O MEGLIO, NEL FRONTE IN CUI IL CLOCK Ë PASSATO DA STATO BASSO (0) A STATO
  //   ALTO(1), L'INGRESSO Ë APERTO ( IL SEGNALE IN D Ë ARRIVATO A QM DI LATCH MASTER)
  //   HALF ADDER:SOMMA DUE BIT CON IL RIPORTO (IL RIPORTO NON VIENE CONSIDERATO COME INGRESSO
  //   R(RIPORTO)= A AND B
  //   D= A XOR B XOR Ping
  //   S3
  //   (A+B)'=A'B'
  //   S(SOMMA)=  A XOR B XOR R
  //   S4
  //   CLEAR = ANNULLA LO STATO 
  //   SET =  SETTA O RESETTA LO STATO
  //   Q
  //   Q'
  //   Q
  //   Q'
  //   A+BC=(A+B)(A+C)
  //   BC
  //   A+B
  //   A+C
  //   A+AB=A
  //   Proprietà DE MORGAN Porta OR
  //   Pout = (A' AND B) OR ( A' AND Ping) OR (B AND Ping)
  //   B
  //   A'
  //   B'
  //   A
  //   Proprietà distributiva della porta AND
  //   A+BC
  //   Proprietà di assorbimento della porta OR
  //   A+AB
  //   R(RIPORTO)= (A AND B) OR (B AND R) OR (A AND R)
  //   S5
  //   (A+B)(A+C)
  //   (A+B)'
  //   A'B'
  //   A=B
  //   A<B
  //   A>B
  //   SLAVE
  //   A+BC
  //   AB+AC
  //   S6
  //   S7
  //   Q
  //   Q'
  //   FINE
endmodule
