// Logisim project Proprietà2bertoldoMatteo.circ as structural Verilog: 1 circuit, main circuit main
module main (
  input  A,
  input  A_2,
  input  B,
  input  B_2,
  input  C,
  input  C_2,
  input  A_3,
  input  A_4,
  input  B_3,
  input  B_4,
  input  C_3,
  input  C_4,
  input  A_5,
  input  A_6,
  input  B_5,
  input  B_6,
  input  A_7,
  input  A_8,
  input  in_19,
  input  in_20,
  input  in_21,
  input  in_22,
  input  in_23,
  input  in_24,
  input  in_25,
  input  in_26,
  input  in_27,
  input  A_9,
  input  B_7,
  input  Ping,
  input  [3:0] INPUT,
  output A_B,
  output AB
);

  wire AB_out, AC_out, and_1_out, and_2_out, and_3_out, and_4_out, and_5_out, and_6_out, and_7_out,
       and_8_out, and_9_out, and_10_out, and_11_out, and_12_out, and_13_out, nand_1_out, nor_1_out,
       not_1_out, not_2_out, not_3_out, not_8_out, not_9_out, or_1_out, or_2_out, or_3_out, or_4_out,
       or_5_out, or_6_out, or_7_out, or_8_out, or_9_out, or_10_out, undriven, xor_1_out, xor_2_out,
       xor_3_out, xor_4_out, xor_5_out;
  wire [3:0] not_7_out;

  or or_1 (or_1_out, B_3, C_3);
  not not_1 (not_1_out, in_19);
  not not_2 (not_2_out, in_21);
  not not_3 (not_3_out, A_9);
  and u_AB (AB_out, A, B);
  and AC (AC_out, A, C_2);
  or or_2 (or_2_out, A_5, B_5);
  // Probe on nand_1_out
  // Probe on nand_1_out
  // Probe on nand_1_out
  // Probe on nand_1_out
  nand nand_1 (nand_1_out, in_19, in_21);
  or or_3 (or_3_out, not_1_out, not_2_out);
  xor xor_1 (xor_1_out, in_25, in_26);
  and and_1 (and_1_out, in_25, in_26);
  and and_2 (and_2_out, in_26, in_27);
  and and_3 (and_3_out, in_27, in_25);
  xor xor_2 (xor_2_out, A_9, B_7);
  not not_4 (not_7_out[3], INPUT[3]);
  not not_5 (not_7_out[2], INPUT[2]);
  not not_6 (not_7_out[1], INPUT[1]);
  not not_7 (not_7_out[0], INPUT[0]);
  // Probe on or_4_out
  or or_4 (or_4_out, AB_out, AC_out);
  // Probe on and_4_out
  and and_4 (and_4_out, A_3, or_1_out);
  // Probe on and_5_out
  // Probe on and_5_out
  and and_5 (and_5_out, A_5, or_2_out);
  // Probe on or_3_out
  // Probe on or_3_out
  // Probe on xor_3_out
  // Probe on xor_3_out
  xor xor_3 (xor_3_out, in_23, in_24);
  // Probe on and_6_out
  // Probe on and_6_out
  and and_6 (and_6_out, in_23, in_24);
  // Probe on xor_4_out
  // Probe on xor_4_out
  xor xor_4 (xor_4_out, xor_2_out, Ping);
  and and_7 (and_7_out, not_3_out, B_7);
  and and_8 (and_8_out, not_3_out, Ping);
  and and_9 (and_9_out, B_7, Ping);
  // Probe on not_7_out
  // Probe on not_7_out
  // Probe on xor_5_out
  // Probe on xor_5_out
  xor xor_5 (xor_5_out, xor_1_out, in_27);
  or or_5 (or_5_out, and_1_out, and_2_out, and_3_out);
  or or_6 (or_6_out, and_7_out, and_8_out, and_9_out);
  // Probe on or_5_out
  // Probe on or_5_out
  // Probe on or_6_out
  // Probe on or_6_out
  nor nor_1 (nor_1_out, in_20, in_22);
  not not_8 (not_8_out, in_20);
  not not_9 (not_9_out, in_22);
  and and_10 (and_10_out, B_2, C);
  or or_7 (or_7_out, A_4, B_4);
  or or_8 (or_8_out, A_4, C_4);
  and and_11 (and_11_out, A_6, B_6);
  // Probe on undriven
  // Probe on undriven
  // Probe on nor_1_out
  // Probe on nor_1_out
  // Probe on nor_1_out
  // Probe on nor_1_out
  and and_12 (and_12_out, not_8_out, not_9_out);
  or or_9 (or_9_out, A_2, and_10_out);
  or or_10 (or_10_out, A_6, and_11_out);
  // Probe on and_12_out
  // Probe on and_12_out
  // Probe on and_12_out
  // Probe on and_12_out
  // Probe on or_9_out
  // Probe on or_9_out
  // Probe on and_13_out
  // Probe on and_13_out
  and and_13 (and_13_out, or_7_out, or_8_out);
  // Probe on or_10_out
  // Probe on or_10_out

  assign A_B = A_7;
  assign AB = A_8;

  // Notes on the sheet:
  //   FINE
  //   B+C
  //   Proprietà distributiva della porta OR
  //   A(B+C)=AB+AC
  //   A(B+C)
  //   Proprietà di assorbimento della porta AND
  //   A(A+B)=A
  //   Proprietà DE MORGAN forma AND
  //   (AB)'=A'+B'
  //   AB+AC
  //   A(A+B)
  //   (AB)'
  //   AB+AC
  //   A(B+C)
  //   A'+B'
  //   DIFFERENZA COMPLETA CON GESTIONE DEL RIPORTO IN INGRESSO E USCITA
  //   COMPLEMENTO A 1 DI 4 BIT IN INPUT
  //   SPLITTER PERMETTE DI SUDDIVIDERE O RAGGRUPPARE UN BUS IN GRUPPI DISTINTI DI BIT
  //   S(SOMMA)= AXOR B
  //   FULL ADDER:SOMMA DUE BIT ( TIENE CONTO DEL RIPORTO IN INGRESSO E USCITA)
  //   HALF ADDER:SOMMA DUE BIT CON IL RIPORTO (IL RIPORTO NON VIENE CONSIDERATO COME INGRESSO
  //   R(RIPORTO)= A AND B
  //   D= A XOR B XOR Ping
  //   (A+B)'=A'B'
  //   S(SOMMA)=  A XOR B XOR R
  //   A+BC=(A+B)(A+C)
  //   BC
  //   A+B
  //   A+C
  //   A+AB=A
  //   Proprietà DE MORGAN Porta OR
  //   Pout = (A' AND B) OR ( A' AND Ping) OR (B AND Ping)
  //   Proprietà distributiva della porta AND
  //   A+BC
  //   Proprietà di assorbimento della porta OR
  //   A+AB
  //   R(RIPORTO)= (A AND B) OR (B AND R) OR (A AND R)
  //   (A+B)(A+C)
  //   (A+B)'
  //   A'B'
  //   A+BC
  //   AB+AC
  //   FINE
endmodule
