// Logisim project Prova1.circ as structural Verilog: 1 circuit, main circuit main
module main (
  input  in_1,
  input  in_2,
  input  in_3,
  input  in_4,
  input  in_5,
  input  in_6,
  input  in_7,
  input  in_8,
  input  in_9,
  input  in_10,
  input  in_11,
  input  in_12,
  input  in_13,
  input  in_14,
  input  in_15,
  input  in_16,
  input  in_17,
  input  in_18,
  input  in_19,
  input  in_20,
  input  in_21,
  input  in_22,
  input  in_23,
  input  in_24,
  input  in_25,
  input  in_26,
  output out_27,
  output out_28,
  output out_29,
  output out_30,
  output out_31,
  output out_32,
  output out_33,
  output out_34,
  output out_35,
  output out_36,
  output out_37
);

  wire and_2_out, nand_1_out, nand_4_out, nand_5_out, nor_1_out, nor_2_out, nor_6_out, not_1_out, not_2_out,
       or_2_out;

  nor nor_1 (nor_1_out, in_25, in_25);
  nor nor_2 (nor_2_out, in_26, in_26);
  // Probe on in_1
  nand nand_1 (nand_1_out, in_19, in_20);
  nor nor_3 (out_35, in_23, in_23);
  nor nor_4 (out_37, nor_1_out, nor_2_out);
  or or_1 (out_30, in_8, in_11);
  and and_1 (out_28, in_3, in_5);
  nand nand_2 (out_31, in_12, in_16);
  and and_2 (and_2_out, in_12, in_16);
  // Probe on not_1_out
  not not_1 (not_1_out, and_2_out);
  nand nand_3 (out_34, nand_1_out, nand_1_out);
  nor nor_5 (out_27, in_2, in_4);
  or or_2 (or_2_out, in_2, in_4);
  // Probe on not_2_out
  not not_2 (not_2_out, or_2_out);
  xor xor_1 (out_29, in_6, in_7, in_9, in_10);
  xnor xnor_1 (out_32, in_13, in_14, in_15, in_17);
  not nand_4 (nand_4_out, in_18);  // NAND_Gate
  not nand_5 (nand_5_out, in_21);  // NAND_Gate
  nor nor_6 (nor_6_out, in_22, in_24);
  not nor_7 (out_36, nor_6_out);  // NOR_Gate
  nand nand_6 (out_33, nand_4_out, nand_4_out, nand_5_out, nand_5_out, nand_5_out);

  // Notes on the sheet:
  //   FINE
  //   PIN/SONDA
  //   CREAZIONE 1 PORTA AND CON 2 PORTE NAND
  //   CREAZIONE PORTA NOT CON 1 PORTA NOR
  //   CREARE UNA PORTA AND UTILIZZANDO 3 PORTE NOR
  //   porta AND
  //   Porta OR
  //   porta NAND
  //   Porta NOR
  //   Porta XOR
  //   Porta XNOR
  //   CREAZIONE PORTA OR CON 3 NAND
  //   CREAZIONE PORTA OR CON 1 PORTA NOR
  //   FINE
endmodule
